# Fritzing sketch robot-rover (saved by Fritzing 0.9.3b)
breadboards: 1

parts:
  LED1 = LED - 5mm [color="White (6500K)" package="5 mm [THT]"]
  LED2 = LED - 5mm [color="White (6500K)" package="5 mm [THT]"]
  LED3 = LED - 5mm [color="Red (633nm)" package="5 mm [THT]"]
  LED4 = LED - 5mm [color="Red (633nm)" package="5 mm [THT]"]
  S1 = Toggle Switch [package=THT]
  R3 = Temperature Sensor (Thermistor) [thermistor_type=NTC package=THT]
  R4 = Resistor [tolerance=±5% resistance=10k package=THT]
  R2 = Resistor [tolerance=±2% resistance=220 package=THT]
  R1 = Resistor [tolerance=±2% resistance=220 package=THT]
  R7 = Photocell (LDR) [package=THT]
  R8 = Resistor [tolerance=±5% resistance=10k package=THT]
  J1 = Piezo Speaker
  Part1 = Adafruit Feather 32u4 Bluefruit [part_number="Adafruit #2829"]

nets:
  N1: LED1.cathode, LED2.cathode, LED3.cathode, LED4.cathode, S1.L1, R3.pin_1, R7.pin_1, Part1.GND
  N2: LED1.anode, LED2.anode, R1.Pin_0
  N3: LED3.anode, LED4.anode, R2.Pin_1
  N4: S1.COM, Part1.EN
  N5: R3.pin_0, R4.Pin_0, Part1.A1
  N6: R4.Pin_1, R8.Pin_0, Part1.+3V3
  N7: R2.Pin_0, Part1.5
  N8: R1.Pin_1, Part1.12
  N9: R7.pin_0, R8.Pin_1, Part1.A3
  N10: J1.pin1, Part1.10
  N11: J1.pin2, Part1.9

custom parts:
  Adafruit Feather 32u4 Bluefruit: This is the Adafruit Feather 32u4 Bluefruit - our take on an 'all-in-one' Arduino-compatible + Bluetooth Low Energy with built in USB and battery charging. Its an Adafruit Feather 32u4 with a BTLE module, ready to rock! We have other boards in the Feather family, check'em out here. Bluetooth Low Energy is the hottest new low-power, 2.4GHz spectrum wireless protocol. In particular, its the only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
